# Fritzing sketch zagruzka-v-arduino-pro-mini (saved by Fritzing 0.9.9b)
breadboards: 1

parts:
  Компонент1 = Arduino Pro Mini (3.3V)
  USB_UART1 = USB-TTL UART

nets:
  N1: Компонент1.DTR, USB_UART1.pin10
  N2: Компонент1.TXO, USB_UART1.pin9
  N3: Компонент1.RXI, USB_UART1.pin8
  N4: Компонент1.VCC, USB_UART1.pin7
  N5: Компонент1.GND, USB_UART1.pin6

custom parts:
  USB-TTL UART: USB programmer interface incorporating Silicon Labs CP2102 UART
