# Fritzing sketch zagruzka-i-sbros (saved by Fritzing 1.0.2b)
breadboards: 1

parts:
  ESP32-CAM1 = ESP32-CAM_tve
  OLED_I2C1 = OLED 128x64 I2C Monochrome Display
  USB_UART1 = USB-TTL UART
  S1 = Square Pushbutton
  S2 = Momentary Switch [package=ksa_sealed_tac_switch]
  R1 = Resistor [tolerance=±5% power=0.25W resistance=10k package=THT]

nets:
  N1: ESP32-CAM1.GPIO14, OLED_I2C1.SDA
  N2: ESP32-CAM1.GPIO13, OLED_I2C1.SCK
  N3: ESP32-CAM1.GPIO0, S1.leg0
  N4: ESP32-CAM1.GND#12, S1.leg1
  N5: ESP32-CAM1.GPIO3_/_RX, USB_UART1.pin8
  N6: ESP32-CAM1.GPIO1_/_TX, USB_UART1.pin9
  N7: ESP32-CAM1.GND#16, S2.2, R1.Pin_0
  N8: OLED_I2C1.VDD, USB_UART1.pin7, R1.Pin_1
  N9: OLED_I2C1.GND, USB_UART1.pin6, S2.4

custom parts:
  ESP32-CAM_tve: The ESP32-CAM has a very competitive small-size camera module that can operate independently as a minimum system with a footprint of only 27*40.5*4.5mm and a deep sleep current of up to 6mA.
  USB-TTL UART: USB programmer interface incorporating Silicon Labs CP2102 UART
